# Fritzing sketch PI_III_schema (saved by Fritzing 0.9.6b)
breadboards: 1

parts:
  A1 = DHT22 module
  part = ESP8266 NodeMCU LoLin module
  R1 = Resistor [tolerance=±5% power=0.25 resistance=220 package=THT]
  OLED_I2C1 = OLED 128x64 I2C Monochrome Display

nets:
  3V3: A1.+, part.3V3, R1.Pin_1, OLED_I2C1.VDD
  N1: A1.Out, part.D3, R1.Pin_0
  GND: A1.-, part.GND, OLED_I2C1.GND
  N2: part.D5, OLED_I2C1.SCK
  N3: part.D6, OLED_I2C1.SDA

custom parts:
  DHT22 module: DHT22 module. Pins VCC Data GND.
  ESP8266 NodeMCU LoLin module: ESP8266 based NodeMCU
